// Digital circuit main.dig as structural Verilog
module main (
  input  in_1,
  input  [31:0] PC,
  input  in_3,
  input  Clock,
  input  [31:0] Write_back,
  input  Write_enable,
  input  Ula_fonte
);

  wire [4:0] multiplexer_1_out;
  wire [31:0] _32x32_1_p7, _32x32_1_p8, bitextender_1_out, instruction_mem_1__32b__out, multiplexer_2_out;

  instruction_mem instruction_mem_1 (._32b__ADDR(PC), ._1b__Enable(in_3), ._32b__Out(instruction_mem_1__32b__out));
  Multiplexer #(.Bits(5)) multiplexer_1 (
    .sel(in_1), .in_0(instruction_mem_1__32b__out[20:16]), .in_1(instruction_mem_1__32b__out[15:11]),
    .out(multiplexer_1_out));
  // _32x32 _32x32_1: pin names not known; wires that end beside it: Write_back, instruction_mem_1__32b__out[25:21], instruction_mem_1__32b__out[20:16], multiplexer_1_out, Clock, Write_enable, _32x32_1_p7, _32x32_1_p8
  BitExtender #(.inputBits(16), .outputBits(32)) bitextender_1 (
    .in(instruction_mem_1__32b__out[15:0]), .out(bitextender_1_out));
  Multiplexer #(.Bits(32)) multiplexer_2 (
    .sel(Ula_fonte), .in_0(_32x32_1_p8), .in_1(bitextender_1_out), .out(multiplexer_2_out));
  ula ula_1 (.ALUControl(4'b0000), .A(_32x32_1_p7), .B(multiplexer_2_out), .Shamt({6{1'b0}}));  // open: Zero, Resultado

  // Other names for the same wires on the sheet: Reg_dest = in_1
endmodule
